// Logisim project MU0.circ as structural Verilog: 6 circuits, main circuit main
module main (
  input  CLK
);

  wire and_1_out, and_2_out, and_3_out, and_4_out, and_5_out, comparator_1_eq, comparator_1_gt, d_ff_1_q,
       decoder_1_out7, decoder_1_out8, decoder_1_out9, decoder_1_out10, decoder_1_out11, decoder_1_out12,
       decoder_1_out13, decoder_1_out14, decoder_1_out15, multiplexer_3_out, not_1_out, not_2_out, not_3_out,
       not_5_out, or_1_out, or_2_out, or_3_out, or_4_out, RST_out, w1, w2, w3, w4, w5, w6, w7, w8;
  wire [3:0] bit_extender_1_out, PC_q, PC_q_2, PC_q_3;
  wire [11:0] adder_1_out, IR_q, multiplexer_1_out, multiplexer_2_out;
  wire [15:0] ACC_q, adder_2_out, multiplexer_4_out, multiplexer_5_out, not_4_out, ram_1_dout;
  wire [15:12] IR_q_2;

  not not_1 (not_1_out, d_ff_1_q);
  Button RST (.out(RST_out));
  Hex_Digit_Display hex_digit_display_1 (.value(PC_q_3));  // open: dp
  Hex_Digit_Display hex_digit_display_2 (.value(PC_q_2));  // open: dp
  or or_1 (or_1_out, and_5_out, w6, and_4_out);
  or or_2 (or_2_out, and_4_out, w6, and_5_out, d_ff_1_q);
  D_Flip_Flop d_ff_1 (.D(not_1_out), .clk(CLK), .Q(d_ff_1_q), .reset(RST_out));  // open: Qn, preset
  Hex_Digit_Display hex_digit_display_3 (.value(PC_q));  // open: dp
  Adder #(.width(12)) adder_1 (
    .a({PC_q_3, PC_q_2, PC_q}), .b({12{1'b0}}), .out(adder_1_out), .cin(1'b1));  // open: cout
  Multiplexer #(.width(12)) multiplexer_1 (.in0(adder_1_out), .in1(IR_q), .out(multiplexer_1_out), .sel(or_1_out));
  and and_1 (and_1_out, or_2_out, w7);
  not not_2 (not_2_out, d_ff_1_q);
  Register #(.width(12)) PC (
    .D(multiplexer_1_out), .en(and_1_out), .clk(CLK), .Q({PC_q_3, PC_q_2, PC_q}), .clr(RST_out));
  Multiplexer #(.width(12)) multiplexer_2 (
    .in0({PC_q_3, PC_q_2, PC_q}), .in1(IR_q), .out(multiplexer_2_out), .sel(d_ff_1_q));
  not not_3 (not_3_out, CLK);
  Multiplexer multiplexer_3 (.in0(1'b0), .in1(1'b1), .out(multiplexer_3_out), .sel(w2));
  Hex_Digit_Display hex_digit_display_4 (.value(multiplexer_2_out[11:8]));  // open: dp
  assign not_4_out = ~ram_1_dout;  // NOT_Gate not_4, 16 bits wide
  Hex_Digit_Display hex_digit_display_5 (.value(multiplexer_2_out[7:4]));  // open: dp
  Hex_Digit_Display hex_digit_display_6 (.value(multiplexer_2_out[3:0]));  // open: dp
  RAM #(.addrWidth(12), .asyncread("true"), .dataWidth(16)) ram_1 (
    .addr(multiplexer_2_out), .we(and_2_out), .oe(1'b1), .clk(CLK), .din(ACC_q), .dout(ram_1_dout));
  and and_2 (and_2_out, w8, not_3_out, d_ff_1_q);
  Multiplexer #(.width(16)) multiplexer_4 (.in0(ACC_q), .in1({16{1'b0}}), .out(multiplexer_4_out), .sel(w1));
  Multiplexer #(.width(16)) multiplexer_5 (
    .in0(ram_1_dout), .in1(not_4_out), .out(multiplexer_5_out), .sel(multiplexer_3_out));
  Adder #(.width(16)) adder_2 (
    .a(multiplexer_4_out), .b(multiplexer_5_out), .out(adder_2_out), .cin(multiplexer_3_out));  // open: cout
  or or_3 (or_3_out, w1, w2, w3);
  and and_3 (and_3_out, or_3_out, d_ff_1_q);
  Register #(.width(16)) ACC (.D(adder_2_out), .en(and_3_out), .clk(CLK), .Q(ACC_q), .clr(RST_out));
  Register #(.width(16)) IR (.D(ram_1_dout), .en(not_2_out), .clk(CLK), .Q({IR_q_2, IR_q}), .clr(RST_out));
  Comparator #(.width(16)) comparator_1 (
    .a(ACC_q), .b({16{1'b0}}), .gt(comparator_1_gt), .eq(comparator_1_eq));  // open: lt
  Hex_Digit_Display hex_digit_display_7 (.value(ACC_q[15:12]));  // open: dp
  Hex_Digit_Display hex_digit_display_8 (.value(ACC_q[11:8]));  // open: dp
  or or_4 (or_4_out, comparator_1_gt, comparator_1_eq);
  not not_5 (not_5_out, comparator_1_eq);
  Hex_Digit_Display hex_digit_display_9 (.value(ACC_q[7:4]));  // open: dp
  Hex_Digit_Display hex_digit_display_10 (.value(ACC_q[3:0]));  // open: dp
  Hex_Digit_Display hex_digit_display_11 (.value(IR_q_2));  // open: dp
  Hex_Digit_Display hex_digit_display_12 (.value(bit_extender_1_out));  // open: dp
  assign bit_extender_1_out = {{3{1'b0}}, d_ff_1_q};  // Bit_Extender bit_extender_1
  Decoder #(.select(4)) decoder_1 (
    .out0(w1), .out1(w8), .out2(w3), .out3(w2), .out4(w6), .out5(w4), .out6(w5), .out7(decoder_1_out7),
    .out8(decoder_1_out8), .out9(decoder_1_out9), .out10(decoder_1_out10), .out11(decoder_1_out11),
    .out12(decoder_1_out12), .out13(decoder_1_out13), .out14(decoder_1_out14), .out15(decoder_1_out15),
    .sel(IR_q_2));  // open: en
  and and_4 (and_4_out, or_4_out, w4);
  and and_5 (and_5_out, not_5_out, w5);
  nor nor_1 (w7, decoder_1_out7, decoder_1_out8, decoder_1_out9, decoder_1_out10, decoder_1_out11, decoder_1_out12, decoder_1_out13, decoder_1_out14, decoder_1_out15);
endmodule

module MUX (
  input  A,
  input  C,
  input  B,
  output out_4
);

  wire not_1_out;

  not not_1 (not_1_out, C);
  // Transmission_Gate transmission_1: pin names not known; wires that end beside it: A, C, not_1_out, out_4
  // Transmission_Gate transmission_2: pin names not known; wires that end beside it: B, not_1_out, C, out_4
endmodule

module Latch (
  input  D,
  input  CLK,
  output O
);

  Multiplexer multiplexer_1 (.in0(O), .in1(D), .out(O), .sel(CLK));
endmodule

module D_FF (
  input  D,
  output Q
);

  wire CLK_out, latch_1_o, not_1_out;

  Clock CLK (.out(CLK_out));
  Latch latch_1 (.D(D), .CLK(CLK_out), .O(latch_1_o));
  not not_1 (not_1_out, CLK_out);
  Latch latch_2 (.D(latch_1_o), .CLK(not_1_out), .O(Q));
endmodule

module Sync_Up_Down_Counter (
  input  Up_Down
);

  wire CLK_out, RST_out;
  wire [3:0] adder_1_out, d_ff_1_q, multiplexer_1_out, not_1_out;

  Clock CLK (.out(CLK_out));
  Button RST (.out(RST_out));
  D_Flip_Flop d_ff_1 (.D(adder_1_out[0]), .clk(CLK_out), .Q(d_ff_1_q[0]), .reset(RST_out));  // open: Qn, preset
  D_Flip_Flop d_ff_2 (.D(adder_1_out[1]), .clk(CLK_out), .Q(d_ff_1_q[1]), .reset(RST_out));  // open: Qn, preset
  D_Flip_Flop d_ff_3 (.D(adder_1_out[2]), .clk(CLK_out), .Q(d_ff_1_q[2]), .reset(RST_out));  // open: Qn, preset
  D_Flip_Flop d_ff_4 (.D(adder_1_out[3]), .clk(CLK_out), .Q(d_ff_1_q[3]), .reset(RST_out));  // open: Qn, preset
  Hex_Digit_Display hex_digit_display_1 (.value(d_ff_1_q));  // open: dp
  Multiplexer #(.width(4)) multiplexer_1 (.in0(4'b0001), .in1(not_1_out), .out(multiplexer_1_out), .sel(Up_Down));
  assign not_1_out = ~4'b0001;  // NOT_Gate not_1, 4 bits wide
  Adder #(.width(4)) adder_1 (.a(d_ff_1_q), .b(multiplexer_1_out), .out(adder_1_out), .cin(Up_Down));  // open: cout
endmodule

module Ripple_Counter (
);

  wire CLK_out, d_ff_1_qn, d_ff_2_qn, d_ff_3_qn, d_ff_4_qn, RST_out;
  wire [3:0] d_ff_1_q;

  Clock CLK (.out(CLK_out));
  Button RST (.out(RST_out));
  D_Flip_Flop d_ff_1 (.D(d_ff_1_qn), .clk(CLK_out), .Q(d_ff_1_q[0]), .Qn(d_ff_1_qn), .reset(RST_out));  // open: preset
  D_Flip_Flop d_ff_2 (
    .D(d_ff_2_qn), .clk(d_ff_1_qn), .Q(d_ff_1_q[1]), .Qn(d_ff_2_qn), .reset(RST_out));  // open: preset
  Hex_Digit_Display hex_digit_display_1 (.value(d_ff_1_q));  // open: dp
  D_Flip_Flop d_ff_3 (
    .D(d_ff_3_qn), .clk(d_ff_2_qn), .Q(d_ff_1_q[2]), .Qn(d_ff_3_qn), .reset(RST_out));  // open: preset
  D_Flip_Flop d_ff_4 (
    .D(d_ff_4_qn), .clk(d_ff_3_qn), .Q(d_ff_1_q[3]), .Qn(d_ff_4_qn), .reset(RST_out));  // open: preset
endmodule
