// Logisim project Booth.circ as structural Verilog: 1 circuit, main circuit main
module main (
  input  [3:0] input1,
  input  [3:0] input2,
  input  start,
  output [7:0] result
);

  wire clk_out, reset_out;
  wire [0:0] Q_1_q;
  wire [1:0] adder_1_out, count_q;
  wire [3:0] adder_2_out, adder_3_out, M, not_1_out;
  wire [8:0] multiplexer_1_out;
  wire [14:0] multiplexer_2_out;

  Clock clk (.out(clk_out));
  Button reset (.out(reset_out));
  Multiplexer #(.select(2), .width(9)) multiplexer_1 (
    .in0({{2{result[7]}}, result[6:0]}), .in1({{2{adder_2_out[3]}}, adder_2_out[2:0], result[3:0]}),
    .in2({{2{adder_3_out[3]}}, adder_3_out[2:0], result[3:0]}), .in3({{2{result[7]}}, result[6:0]}),
    .out(multiplexer_1_out), .sel({result[0], Q_1_q[0]}));
  Multiplexer #(.width(15)) multiplexer_2 (
    .in0({4'b0000, input1, input2, 3'b000}),
    .in1({multiplexer_1_out[8:5], M, multiplexer_1_out[4:0], adder_1_out}), .out(multiplexer_2_out),
    .sel(start));
  Register #(.width(4)) A (.D(multiplexer_2_out[14:11]), .en(1'b1), .clk(clk_out), .Q(result[7:4]), .clr(reset_out));
  Register #(.width(4)) u_M (.D(multiplexer_2_out[10:7]), .en(1'b1), .clk(clk_out), .Q(M), .clr(reset_out));
  Register #(.width(4)) Q (.D(multiplexer_2_out[6:3]), .en(1'b1), .clk(clk_out), .Q(result[3:0]), .clr(reset_out));
  Register #(.width(1)) Q_1 (.D(multiplexer_2_out[2]), .en(1'b1), .clk(clk_out), .Q(Q_1_q[0]), .clr(reset_out));
  Register #(.width(2)) count (.D(multiplexer_2_out[1:0]), .en(1'b1), .clk(clk_out), .Q(count_q), .clr(reset_out));
  assign not_1_out = ~M;  // NOT_Gate not_1, 4 bits wide
  Adder #(.width(2)) adder_1 (.a(count_q), .b(2'b00), .out(adder_1_out), .cin(1'b1));  // open: cout
  Adder #(.width(4)) adder_2 (.a(result[7:4]), .b(M), .out(adder_2_out), .cin(1'b0));  // open: cout
  Adder #(.width(4)) adder_3 (.a(result[7:4]), .b(not_1_out), .out(adder_3_out), .cin(1'b1));  // open: cout
  // Probe on M
  // Probe on result[3:0]
  // Probe on result[7:4]
  // Probe on Q_1_q[0]

  // Notes on the sheet:
  //   add
  //   sub
endmodule
